// Logisim project Updated.circ as structural Verilog: 12 circuits, main circuit Computer
module Computer (
);

  wire clock_2_out, clock_3_out, cpu_1_data_write_e, cpu_1_mem_write_e, joystickcontroller_1_joystickwrite,
       keyboard_1_avail, keyboardcontroller_1_databuswrite, keyboardcontroller_1_keyboardread,
       memory_1_data_bus_write_e, rgb_video_1_p1, rgb_video_1_p2, terminalcontroller_1_terminal_we;
  wire [3:0] joystick_1_x, joystick_1_y;
  wire [5:0] rgb_video_1_p3, rgb_video_1_p4;
  wire [6:0] keyboard_1_data, terminalcontroller_1_databus_out;
  wire [15:0] cpu_1_address;
  wire [23:0] rgb_video_1_p5;
  wire [31:0] controlled_buffer_1_out, cpu_1_data_bus, joystickcontroller_1_databus,
       keyboardcontroller_1_databusout, memory_1_data_bus_out;

  Joystick joystick_1 (.x(joystick_1_x), .y(joystick_1_y));
  // Probe on cpu_1_address
  // RGB_Video #(.height(64), .scale(1), .width(64)) rgb_video_1: pin names not known; wires that end beside it: rgb_video_1_p1, rgb_video_1_p2, rgb_video_1_p3, rgb_video_1_p4, rgb_video_1_p5
  Clock clock_1 (.out(rgb_video_1_p1));
  TTY tty_1 (
    .data(terminalcontroller_1_databus_out), .clk(clock_2_out), .we(terminalcontroller_1_terminal_we));  // open: clr
  Clock clock_2 (.out(clock_2_out));
  Clock clock_3 (.out(clock_3_out));
  CPU cpu_1 (
    .Data_bus_in(controlled_buffer_1_out), .Address(cpu_1_address), .Mem_write_e(cpu_1_mem_write_e),
    .Data_bus(cpu_1_data_bus), .Data_write_e(cpu_1_data_write_e));
  Keyboard keyboard_1 (
    .clk(clock_3_out), .re(keyboardcontroller_1_keyboardread), .avail(keyboard_1_avail),
    .data(keyboard_1_data));  // open: clr
  assign controlled_buffer_1_out = memory_1_data_bus_write_e ? memory_1_data_bus_out : 32'bz;  // Controlled_Buffer controlled_buffer_1
  Memory memory_1 (
    .Address(cpu_1_address), .Write_e(cpu_1_data_write_e), .Data_Bus_in(controlled_buffer_1_out),
    .Data_Bus_out(memory_1_data_bus_out), .Data_Bus_Write_e(memory_1_data_bus_write_e));
  assign controlled_buffer_1_out = cpu_1_mem_write_e ? cpu_1_data_bus : 32'bz;  // Controlled_Buffer controlled_buffer_2
  assign controlled_buffer_1_out = keyboardcontroller_1_databuswrite ? keyboardcontroller_1_databusout : 32'bz;  // Controlled_Buffer controlled_buffer_3
  KeyboardController keyboardcontroller_1 (
    .DataBusIn(controlled_buffer_1_out), .WriteEnable(cpu_1_data_write_e), .AddressIn(cpu_1_address),
    .KeyboardIn(keyboard_1_data), .KeyboardKeyPressAvailable(keyboard_1_avail),
    .DataBusOut(keyboardcontroller_1_databusout), .DataBusWrite(keyboardcontroller_1_databuswrite),
    .KeyboardRead(keyboardcontroller_1_keyboardread));
  assign controlled_buffer_1_out = joystickcontroller_1_joystickwrite ? joystickcontroller_1_databus : 32'bz;  // Controlled_Buffer controlled_buffer_4
  JoystickController joystickcontroller_1 (
    .Xcoord(joystick_1_x), .Ycoord(joystick_1_y), .Address(cpu_1_address),
    .Databus(joystickcontroller_1_databus), .JoystickWrite(joystickcontroller_1_joystickwrite));
  RGBController rgbcontroller_1 (
    .AddressIn(cpu_1_address), .DataBusIn(controlled_buffer_1_out), .WriteEnable(cpu_1_data_write_e),
    .RGBX(rgb_video_1_p3), .RGBY(rgb_video_1_p4), .RGBColor(rgb_video_1_p5), .RGBWrite(rgb_video_1_p2));
  TerminalController terminalcontroller_1 (
    .DataBus_in(controlled_buffer_1_out), .Address_in(cpu_1_address), .DataBus_we(cpu_1_data_write_e),
    .DataBus_out(terminalcontroller_1_databus_out), .Terminal_we(terminalcontroller_1_terminal_we));

  // Notes on the sheet:
  //   Data
  //   Address
  //   Write_enable
endmodule

module CPU (
  input  [31:0] Data_bus_in,
  output [15:0] Address,
  output Mem_write_e,
  output [31:0] Data_bus,
  output Data_write_e
);

  wire alu_1_equal, and_1_out, and_2_out, clock_1_out, control_1_beq_select, control_1_bne_select,
       control_1_imm_sel, control_1_j_select, control_1_jal_select, control_1_jalr_select,
       control_1_jr_select, control_1_lw_select, control_1_shift_select, control_1_we_regfil, not_1_out,
       or_1_out, or_2_out, or_3_out, or_4_out;
  wire [3:0] control_1_op_code;
  wire [4:0] control_1_rd_select, control_1_rs_select, control_1_rt_select, control_1_shift_amounts;
  wire [15:0] bit_extender_3_out, control_1_imm, shifter_1_out;
  wire [25:0] bit_extender_4_out, shifter_2_out;
  wire [31:0] adder_1_out, adder_2_out, alu_1_res, bit_extender_1_out, bit_extender_2_out,
       bit_extender_5_out, bit_extender_6_out, multiplexer_1_out, multiplexer_2_out, multiplexer_3_out,
       multiplexer_4_out, multiplexer_5_out, multiplexer_6_out, multiplexer_7_out, ProgramCounter_q,
       regfile_1_data_rs, rom_1_data, shifter_3_out;

  // Probe on adder_2_out
  Adder #(.width(32)) adder_1 (.a(ProgramCounter_q), .b(32'h4), .out(adder_1_out));  // open: cin, cout
  assign bit_extender_1_out = {{16{shifter_1_out[15]}}, shifter_1_out};  // Bit_Extender bit_extender_1
  Shifter #(.width(16)) shifter_1 (.in(control_1_imm), .\dist (4'b0010), .out(shifter_1_out));
  // Probe on adder_1_out
  Adder #(.width(32)) adder_2 (.a(adder_1_out), .b(bit_extender_1_out), .out(adder_2_out));  // open: cin, cout
  Shifter #(.width(26)) shifter_2 (.in(bit_extender_4_out), .\dist (5'b00010), .out(shifter_2_out));
  assign bit_extender_2_out = {{6{shifter_2_out[25]}}, shifter_2_out};  // Bit_Extender bit_extender_2
  Multiplexer #(.width(32)) multiplexer_1 (
    .in0(adder_1_out), .in1(adder_2_out), .out(multiplexer_1_out), .sel(or_1_out));
  Multiplexer #(.width(32)) multiplexer_2 (
    .in0(bit_extender_2_out), .in1(regfile_1_data_rs), .out(multiplexer_2_out), .sel(or_4_out));
  Multiplexer #(.width(32)) multiplexer_3 (
    .in0(multiplexer_1_out), .in1(multiplexer_2_out), .out(multiplexer_3_out), .sel(or_2_out));
  Register #(.width(32)) ProgramCounter (
    .D(multiplexer_3_out), .en(1'b1), .clk(clock_1_out), .Q(ProgramCounter_q));  // open: clr
  Clock clock_1 (.out(clock_1_out));
  Shifter #(.shift("lr"), .width(32)) shifter_3 (.in(ProgramCounter_q), .\dist (5'b00010), .out(shifter_3_out));
  ROM #(.addrWidth(16), .dataWidth(32)) rom_1 (.addr(bit_extender_3_out), .data(rom_1_data));
  Bit_Extender #(.in_width(32)) bit_extender_3 (.in(shifter_3_out), .out(bit_extender_3_out));
  Bit_Extender #(.in_width(32), .out_width(26)) bit_extender_4 (.in(rom_1_data), .out(bit_extender_4_out));
  // Probe on rom_1_data
  // Probe on regfile_1_data_rs
  // Probe on multiplexer_7_out
  // Probe on multiplexer_5_out
  Multiplexer #(.width(32)) multiplexer_4 (
    .in0(alu_1_res), .in1(Data_bus_in), .out(multiplexer_4_out), .sel(control_1_lw_select));
  or or_1 (or_1_out, and_1_out, and_2_out);
  Multiplexer #(.width(32)) multiplexer_5 (
    .in0(multiplexer_4_out), .in1(adder_1_out), .out(multiplexer_5_out), .sel(or_3_out));
  // Probe on control_1_rd_select
  // Probe on control_1_rd_select
  or or_2 (or_2_out, or_4_out, control_1_j_select, or_3_out);
  regfile regfile_1 (
    .w_e(control_1_we_regfil), .rs(control_1_rs_select), .rd(control_1_rd_select),
    .data_in(multiplexer_5_out), .rt(control_1_rt_select), .data_rs(regfile_1_data_rs), .data_rt(Data_bus));
  Control control_1 (
    .Instruction(rom_1_data), .lw_select(control_1_lw_select), .sw_select(Data_write_e),
    .j_select(control_1_j_select), .jal_select(control_1_jal_select), .jr_select(control_1_jr_select),
    .jalr_select(control_1_jalr_select), .beq_select(control_1_beq_select),
    .bne_select(control_1_bne_select), .imm_sel(control_1_imm_sel), .rs_select(control_1_rs_select),
    .rt_select(control_1_rt_select), .imm(control_1_imm), .rd_select(control_1_rd_select),
    .we_regfil(control_1_we_regfil), .shift_amounts(control_1_shift_amounts), .op_code(control_1_op_code),
    .shift_select(control_1_shift_select));
  or or_3 (or_3_out, control_1_jal_select, control_1_jalr_select);
  // Probe on regfile_1_data_rs
  // Probe on control_1_rs_select
  assign bit_extender_5_out = {{16{control_1_imm[15]}}, control_1_imm};  // Bit_Extender bit_extender_5
  or or_4 (or_4_out, control_1_jr_select, control_1_jalr_select);
  // Probe on control_1_rt_select
  Multiplexer #(.width(32)) multiplexer_6 (
    .in0(Data_bus), .in1(bit_extender_5_out), .out(multiplexer_6_out), .sel(control_1_imm_sel));
  and and_1 (and_1_out, not_1_out, control_1_bne_select);
  and and_2 (and_2_out, alu_1_equal, control_1_beq_select);
  not not_1 (not_1_out, alu_1_equal);
  assign bit_extender_6_out = {{27{control_1_shift_amounts[4]}}, control_1_shift_amounts};  // Bit_Extender bit_extender_6
  Multiplexer #(.width(32)) multiplexer_7 (
    .in0(multiplexer_6_out), .in1(bit_extender_6_out), .out(multiplexer_7_out), .sel(control_1_shift_select));
  // Probe on multiplexer_7_out
  ALU alu_1 (
    .operation(control_1_op_code), .op1(regfile_1_data_rs), .op2(multiplexer_7_out), .res(alu_1_res),
    .equal(alu_1_equal));
  // Probe on alu_1_res
  // Probe on alu_1_res
  Bit_Extender #(.in_width(32)) bit_extender_7 (.in(alu_1_res), .out(Address));

  assign Mem_write_e = Data_write_e;

  // Notes on the sheet:
  //   PC+4
  //   PC+4+offset
  //   if branches is to be taken
  //   label
  //   jr/jalr
  //   jr/jalr
  //   any j*
  //   rs_data for jr and jalr
  //   label to jump to for j and jal
  //   immediate, offset for beq and bne
  //   contents of rom_1 (hex, n*v repeats v):
  //   10400063 201b000a 105b000a 201b000c 105b000a 201b0050 105b004b 201b0005 105b000d 201b004d 105b004c
  //   201b0041 105b004c 800000d 3400008 8c1b0010 13600003 8c020014 ac000010 8000015 20020000 3400008
  //   23bdfffc afa80000 20030000 23bdfffc afba0000 2002000c c 8fba0000 23bd0004 1040fff9 20080020 1048002c
  //   10600003 201b000a 7b0018 1812 201b0030 145b0002 20630000 800004d 237b0001 145b0002 20630001 800004d
  //   237b0001 145b0002 20630002 800004d 237b0001 145b0002 20630003 800004d 237b0001 145b0002 20630004
  //   800004d 237b0001 145b0002 20630005 800004d 237b0001 145b0002 20630006 800004d 237b0001 145b0002
  //   20630007 800004d 237b0001 145b0002 20630008 800004d 237b0001 145b0002 20630009 8000019 20620000
  //   8fa80000 23bd0004 3400008 ac040020 ac050024 ac060028 ac00002c 3400008 ac040070 3400008 23bdfff8
  //   afa80000 afa90004 8c080030 8c090034 21020000 21230000 8fa80000 8fa90004 23bd0008 3400008 20090001
  //   ac09002c 23bdc000 20100000 20110000 20120001 20130000 20140100 20150040 20020005 c 200e0001 104e0005
  //   200e0002 104e0025 200e0003 104e0066 800016b 23ae0000 23bdffe8 afa80000 afa90004 afac0008 afad000c
  //   afaa0010 afab0014 2008000a 2009003f 200c00ff 200d0028 112d000d 85180 1495020 14e5020 a5080 200b0001
  //   ad4b0000 20020050 82020 92820 c3020 c 2129ffff 8000082 8fa80000 8fa90004 8fac0008 8fad000c 8faa0010
  //   8fab0014 23bd0018 800013f 23ae0000 23bdffe8 afa80000 afa90004 afac0008 afad000c afaa0010 afab0014
  //   2008000a 2009003f 200c00ff 200d0028 112d000d 85180 1495020 14e5020 a5080 200b0001 ad4b0000 20020050
  //   82020 92820 c3020 c 2129ffff 80000a4 8fa80000 8fa90004 8fac0008 8fad000c 8faa0010 8fab0014 23bd0018
  //   23ae0000 23bdffe8 afa80000 afa90004 afac0008 afad000c afaa0010 afab0014 2008003f 2009000f 200c00ff
  //   200d0023 110d000d 85180 1495020 14e5020 a5080 200b0001 ad4b0000 20020050 82020 92820 c3020 c
  //   2108ffff 80000c5 8fa80000 8fa90004 8fac0008 8fad000c 8faa0010 8fab0014 23bd0018 800013f 23ae0000
  //   23bdffe8 afa80000 afa90004 afac0008 afad000c afaa0010 afab0014 2008000a 2009003f 200c00ff 200d0028
  //   112d000d 85180 1495020 14e5020 a5080 200b0001 ad4b0000 20020050 82020 92820 c3020 c 2129ffff 80000e7
  //   8fa80000 8fa90004 8fac0008 8fad000c 8faa0010 8fab0014 23bd0018 23ae0000 23bdffe8 afa80000 afa90004
  //   afac0008 afad000c afaa0010 afab0014 2008003f 2009000f 200c00ff 200d0023 110d000d 85180 1495020
  //   14e5020 a5080 200b0001 ad4b0000 20020050 82020 92820 c3020 c 2108ffff 8000108 8fa80000 8fa90004
  //   8fac0008 8fad000c 8faa0010 8fab0014 23bd0018 23ae0000 23bdffe8 afa80000 afa90004 afac0008 afad000c
  //   afaa0010 afab0014 20080023 20090032 200c00ff 200d0023 112d000d 85180 1495020 14e5020 a5080 200b0001
  //   ad4b0000 20020050 82020 92820 c3020 c 2129ffff 8000129 8fa80000 8fa90004 8fac0008 8fad000c 8faa0010
  //   8fab0014 23bd0018 800013f 20020041 c 2008000f 200b0001 14480003 146b0002 20120000 2013ffff 144b0003
  //   146b0002 2012ffff 20130000 14480003 14680002 20120001 20130000 144b0003 14680002 20120000 20130001
  //   2128020 2338820 104180 1114020 11d4020 84080 8d0a0000 20090001 1149000f 200502a 1149000d 215502a
  //   200f0001 1ea5022 1149000b 220502a 11490009 235502a 200f0001 1ea5022 11490007 ad090000 20020050
  //   102020 112820 143020 c 800013f 23bd4000 2002000a c
  //   jal and jalr
  //   all jumps
  //   beq and equal
  //   bne and not equal
endmodule

module Memory (
  input  [15:0] Address,
  input  Write_e,
  input  [31:0] Data_Bus_in,
  output [31:0] Data_Bus_out,
  output Data_Bus_Write_e
);

  wire and_2_out, clock_1_out, comparator_1_eq, comparator_1_gt, not_1_out, or_1_out;
  wire [15:0] shifter_1_out;

  Comparator #(.mode("unsigned"), .width(16)) comparator_1 (
    .a(Address), .b(16'h100), .gt(comparator_1_gt), .eq(comparator_1_eq));  // open: lt
  or or_1 (or_1_out, comparator_1_gt, comparator_1_eq);
  not not_1 (not_1_out, Write_e);
  and and_1 (Data_Bus_Write_e, or_1_out, not_1_out);
  Shifter #(.shift("lr"), .width(16)) shifter_1 (.in(Address), .\dist (4'b0010), .out(shifter_1_out));
  and and_2 (and_2_out, Write_e, or_1_out);
  RAM #(.addrWidth(16), .dataWidth(32), .enables("line")) ram_1 (
    .addr(shifter_1_out), .we(and_2_out), .clk(clock_1_out), .din(Data_Bus_in), .dout(Data_Bus_out));
  Clock clock_1 (.out(clock_1_out));

  // Notes on the sheet:
  //   More logic needed to determine WHEN you read/writing from mem and when you need to write to the bus
endmodule

module KeyboardController (
  input  [31:0] DataBusIn,
  input  WriteEnable,
  input  [15:0] AddressIn,
  input  [6:0] KeyboardIn,
  input  KeyboardKeyPressAvailable,
  output [31:0] DataBusOut,
  output DataBusWrite,
  output KeyboardRead
);

  wire and_2_out, comparator_1_eq, comparator_2_eq, comparator_3_eq, not_1_out, not_2_out, or_1_out;
  wire [31:0] bit_extender_1_out, bit_extender_2_out;

  Comparator #(.width(16)) comparator_1 (.a(AddressIn), .b(16'h10), .eq(comparator_1_eq));  // open: gt, lt
  Comparator #(.width(16)) comparator_2 (.a(AddressIn), .b(16'h14), .eq(comparator_2_eq));  // open: gt, lt
  assign bit_extender_1_out = {{25{1'b0}}, KeyboardIn};  // Bit_Extender bit_extender_1
  assign bit_extender_2_out = {{31{1'b0}}, KeyboardKeyPressAvailable};  // Bit_Extender bit_extender_2
  Comparator #(.width(32)) comparator_3 (.a(DataBusIn), .b({32{1'b0}}), .eq(comparator_3_eq));  // open: gt, lt
  not not_1 (not_1_out, WriteEnable);
  and and_1 (KeyboardRead, comparator_3_eq, WriteEnable, comparator_1_eq);
  and and_2 (and_2_out, comparator_2_eq, not_1_out);
  Multiplexer #(.width(32)) multiplexer_1 (
    .in0(bit_extender_2_out), .in1(bit_extender_1_out), .out(DataBusOut), .sel(and_2_out));
  not not_2 (not_2_out, WriteEnable);
  or or_1 (or_1_out, comparator_1_eq, comparator_2_eq);
  and and_3 (DataBusWrite, not_2_out, or_1_out);
endmodule

module RGBController (
  input  [15:0] AddressIn,
  input  [31:0] DataBusIn,
  input  WriteEnable,
  output [5:0] RGBX,
  output [5:0] RGBY,
  output [23:0] RGBColor,
  output RGBWrite
);

  wire and_1_out, and_2_out, and_3_out, clock_1_out, clock_2_out, clock_3_out, comparator_1_eq,
       comparator_2_eq, comparator_3_eq, comparator_4_eq;
  wire [31:0] register_1_q, register_2_q, register_3_q;

  Comparator #(.width(16)) comparator_1 (.a(AddressIn), .b(16'h20), .eq(comparator_1_eq));  // open: gt, lt
  Comparator #(.width(16)) comparator_2 (.a(AddressIn), .b(16'h24), .eq(comparator_2_eq));  // open: gt, lt
  Comparator #(.width(16)) comparator_3 (.a(AddressIn), .b(16'h28), .eq(comparator_3_eq));  // open: gt, lt
  Comparator #(.width(16)) comparator_4 (.a(AddressIn), .b(16'h2c), .eq(comparator_4_eq));  // open: gt, lt
  and and_1 (and_1_out, comparator_1_eq, WriteEnable);
  and and_2 (and_2_out, comparator_2_eq, WriteEnable);
  and and_3 (and_3_out, comparator_3_eq, WriteEnable);
  and and_4 (RGBWrite, comparator_4_eq, WriteEnable);
  Register #(.width(32)) register_1 (.D(DataBusIn), .en(and_1_out), .clk(clock_1_out), .Q(register_1_q));  // open: clr
  Clock clock_1 (.out(clock_1_out));
  Register #(.width(32)) register_2 (.D(DataBusIn), .en(and_2_out), .clk(clock_2_out), .Q(register_2_q));  // open: clr
  Clock clock_2 (.out(clock_2_out));
  Register #(.width(32)) register_3 (.D(DataBusIn), .en(and_3_out), .clk(clock_3_out), .Q(register_3_q));  // open: clr
  Clock clock_3 (.out(clock_3_out));
  Bit_Extender #(.in_width(32), .out_width(6)) bit_extender_1 (.in(register_1_q), .out(RGBX));
  Bit_Extender #(.in_width(32), .out_width(6)) bit_extender_2 (.in(register_2_q), .out(RGBY));
  Bit_Extender #(.in_width(32), .out_width(24)) bit_extender_3 (.in(register_3_q), .out(RGBColor));
endmodule

module ALU (
  input  [3:0] operation,
  input  [31:0] op1,
  input  [31:0] op2,
  output [31:0] res,
  output equal
);

  wire and_1_out, and_2_out, and_3_out, clock_1_out, clock_2_out, comparator_1_lt, comparator_2_eq,
       comparator_3_eq, not_1_out, not_2_out, or_1_out, or_2_out;
  wire [4:0] bit_extender_1_out, bit_extender_2_out;
  wire [5:0] clo_1_out_2, clz_1_out_2, multiplexer_6_out;
  wire [31:0] adder_1_out, bit_extender_3_out, bit_extender_4_out, divider_1_out, divider_1_rem, HI_q, LO_q,
       multiplexer_1_out, multiplexer_2_out, multiplexer_3_out, multiplexer_4_out, multiplexer_5_out,
       multiplexer_7_out, multiplexer_8_out, multiplexer_9_out, multiplexer_10_out, multiplier_1_cout,
       multiplier_1_out, shifter_1_out, shifter_2_out, subtractor_1_out;

  Bit_Extender #(.in_width(32), .out_width(5)) bit_extender_1 (.in(op2), .out(bit_extender_1_out));
  Bit_Extender #(.in_width(32), .out_width(5)) bit_extender_2 (.in(op2), .out(bit_extender_2_out));
  Adder #(.width(32)) adder_1 (.a(op1), .b(op2), .out(adder_1_out));  // open: cin, cout
  Subtractor #(.width(32)) subtractor_1 (.a(op1), .b(op2), .out(subtractor_1_out));  // open: bin, bout
  Shifter #(.width(32)) shifter_1 (.in(op1), .\dist (bit_extender_1_out), .out(shifter_1_out));
  Shifter #(.shift("lr"), .width(32)) shifter_2 (.in(op1), .\dist (bit_extender_2_out), .out(shifter_2_out));
  // Probe on equal
  Comparator #(.width(32)) comparator_1 (.a(op1), .b(op2), .eq(equal), .lt(comparator_1_lt));  // open: gt
  Multiplexer #(.width(32)) multiplexer_1 (
    .in0(adder_1_out), .in1(subtractor_1_out), .out(multiplexer_1_out), .sel(operation[0]));
  Multiplexer #(.width(32)) multiplexer_2 (
    .in0(shifter_1_out), .in1(shifter_2_out), .out(multiplexer_2_out), .sel(operation[0]));
  clz clz_1 (.in_1(op1), .out_2(clz_1_out_2));
  clo clo_1 (.in_1(op1), .out_2(clo_1_out_2));
  assign bit_extender_3_out = {{31{1'b0}}, comparator_1_lt};  // Bit_Extender bit_extender_3
  Comparator #(.width(4)) comparator_2 (.a(4'b1110), .b(operation), .eq(comparator_2_eq));  // open: gt, lt
  Comparator #(.width(4)) comparator_3 (.a(4'b1111), .b(operation), .eq(comparator_3_eq));  // open: gt, lt
  // Probe on bit_extender_3_out
  Multiplexer #(.width(32)) multiplexer_3 (.in0(LO_q), .in1(HI_q), .out(multiplexer_3_out), .sel(operation[0]));
  Multiplexer #(.width(32)) multiplexer_4 (
    .in0(multiplexer_2_out), .in1(multiplexer_3_out), .out(multiplexer_4_out), .sel(operation[1]));
  or or_1 (or_1_out, comparator_2_eq, comparator_3_eq);
  Multiplexer #(.width(32)) multiplexer_5 (
    .in0(multiplexer_1_out), .in1(multiplexer_4_out), .out(multiplexer_5_out), .sel(operation[2]));
  Multiplexer #(.width(6)) multiplexer_6 (
    .in0(clz_1_out_2), .in1(clo_1_out_2), .out(multiplexer_6_out), .sel(operation[0]));
  Multiplexer #(.width(32)) multiplexer_7 (
    .in0(multiplexer_5_out), .in1(bit_extender_3_out), .out(multiplexer_7_out), .sel(operation[3]));
  not not_1 (not_1_out, operation[2]);
  assign bit_extender_4_out = {{26{1'b0}}, multiplexer_6_out};  // Bit_Extender bit_extender_4
  // Probe on multiplexer_6_out
  and and_1 (and_1_out, not_1_out, operation[1]);
  not not_2 (not_2_out, operation[0]);
  and and_2 (and_2_out, and_1_out, operation[0]);
  and and_3 (and_3_out, and_1_out, not_2_out);
  Multiplexer #(.width(32)) multiplexer_8 (
    .in0(multiplexer_7_out), .out(multiplexer_8_out), .sel(or_2_out));  // open: in1
  // Probe on multiplexer_8_out
  or or_2 (or_2_out, and_2_out, and_3_out);
  Divider #(.width(32)) divider_1 (.a(op1), .b(op2), .out(divider_1_out), .rem(divider_1_rem));  // open: upper
  Multiplier #(.width(32)) multiplier_1 (
    .a(op1), .b(op2), .out(multiplier_1_out), .cout(multiplier_1_cout));  // open: cin
  Multiplexer #(.width(32)) multiplexer_9 (
    .in0(divider_1_out), .in1(multiplier_1_out), .out(multiplexer_9_out), .sel(and_3_out));
  Multiplexer #(.width(32)) multiplexer_10 (
    .in0(multiplier_1_cout), .in1(divider_1_rem), .out(multiplexer_10_out), .sel(and_2_out));
  Clock clock_1 (.out(clock_1_out));
  Register #(.width(32)) HI (.D(multiplexer_10_out), .en(or_2_out), .clk(clock_2_out), .Q(HI_q));  // open: clr
  Clock clock_2 (.out(clock_2_out));
  Register #(.width(32)) LO (.D(multiplexer_9_out), .en(or_2_out), .clk(clock_1_out), .Q(LO_q));  // open: clr
  Multiplexer #(.width(32)) multiplexer_11 (
    .in0(multiplexer_8_out), .in1(bit_extender_4_out), .out(res), .sel(or_1_out));
endmodule

module Control (
  input  [31:0] Instruction,
  output lw_select,
  output sw_select,
  output j_select,
  output jal_select,
  output jr_select,
  output jalr_select,
  output beq_select,
  output bne_select,
  output imm_sel,
  output [4:0] rs_select,
  output [4:0] rt_select,
  output [15:0] imm,
  output [4:0] rd_select,
  output we_regfil,
  output [4:0] shift_amounts,
  output [3:0] op_code,
  output shift_select
);

  wire and_1_out, and_2_out, and_3_out, and_4_out, and_5_out, and_6_out, and_7_out, and_8_out, and_9_out,
       and_10_out, and_11_out, and_12_out, and_13_out, and_14_out, and_16_out, demultiplexer_4_out1,
       demultiplexer_5_out0, demultiplexer_5_out1, demultiplexer_6_out0, demultiplexer_6_out1,
       demultiplexer_7_out0, demultiplexer_7_out1, demultiplexer_8_out0, demultiplexer_8_out1, not_1_out,
       not_2_out, not_3_out, not_4_out, not_5_out, not_6_out, not_7_out, not_8_out, not_9_out, not_10_out,
       not_11_out, not_12_out, not_13_out, not_14_out, not_15_out, not_16_out, not_17_out, not_18_out,
       not_19_out, not_20_out, not_21_out, not_22_out, not_23_out, not_24_out, not_25_out, not_26_out,
       not_27_out, not_28_out, not_29_out, not_30_out, not_31_out, not_32_out, not_33_out, not_34_out,
       not_35_out, not_36_out, not_37_out, not_38_out, not_39_out, not_40_out, not_41_out, not_42_out,
       not_43_out, not_44_out, not_45_out, not_46_out, not_47_out, not_48_out, not_49_out, not_50_out,
       not_51_out, or_1_out, or_2_out, or_5_out, or_7_out, or_8_out, or_9_out, or_11_out, or_12_out,
       or_13_out, undriven;
  wire [4:0] multiplexer_4_out, multiplexer_6_out;

  // Probe on Instruction
  and and_1 (and_1_out, ~Instruction[31], Instruction[30], Instruction[29], Instruction[28], ~Instruction[27], ~Instruction[26], Instruction[5], ~Instruction[4], ~Instruction[3], ~Instruction[2], ~Instruction[1]);  // AND_Gate
  and and_2 (and_2_out, and_1_out, not_1_out);
  not not_1 (not_1_out, Instruction[0]);
  or or_1 (or_1_out, and_2_out, and_3_out);
  not not_2 (not_2_out, Instruction[5]);
  not not_3 (not_3_out, Instruction[6]);
  and and_3 (and_3_out, and_1_out, Instruction[0]);
  not not_4 (not_4_out, Instruction[31]);
  not not_5 (not_5_out, Instruction[30]);
  not not_6 (not_6_out, Instruction[29]);
  not not_7 (not_7_out, Instruction[0]);
  not not_8 (not_8_out, Instruction[1]);
  and and_4 (and_4_out, not_3_out, not_2_out, Instruction[3], Instruction[2], not_8_out, not_7_out, and_5_out);
  and and_5 (and_5_out, not_4_out, not_5_out, not_6_out, not_10_out, not_11_out, not_9_out);
  not not_9 (not_9_out, Instruction[26]);
  not not_10 (not_10_out, Instruction[28]);
  not not_11 (not_11_out, Instruction[27]);
  not not_12 (not_12_out, Instruction[30]);
  and and_6 (and_6_out, Instruction[31], not_12_out, not_13_out, Instruction[27], Instruction[26]);
  not not_13 (not_13_out, Instruction[28]);
  and and_7 (and_7_out, not_14_out, not_16_out, not_17_out, not_15_out, Instruction[27]);
  not not_14 (not_14_out, Instruction[31]);
  not not_15 (not_15_out, Instruction[28]);
  not not_16 (not_16_out, Instruction[30]);
  not not_17 (not_17_out, Instruction[29]);
  not not_18 (not_18_out, Instruction[31]);
  or or_2 (or_2_out, and_6_out, and_8_out);
  and and_8 (and_8_out, not_18_out, not_20_out, not_19_out, Instruction[28], not_21_out);
  not not_19 (not_19_out, Instruction[29]);
  not not_20 (not_20_out, Instruction[30]);
  not not_21 (not_21_out, Instruction[27]);
  Demultiplexer demultiplexer_1 (.out0(lw_select), .out1(sw_select), .in(and_6_out), .sel(Instruction[29]));
  Demultiplexer demultiplexer_2 (.out0(j_select), .out1(jal_select), .in(and_7_out), .sel(Instruction[26]));
  not not_22 (not_22_out, Instruction[4]);
  not not_23 (not_23_out, Instruction[5]);
  and and_9 (and_9_out, and_5_out, not_23_out, not_22_out, Instruction[3], not_25_out, not_24_out);
  Demultiplexer demultiplexer_3 (.out0(beq_select), .out1(bne_select), .in(and_8_out), .sel(Instruction[26]));
  not not_24 (not_24_out, Instruction[1]);
  not not_25 (not_25_out, Instruction[2]);
  and and_10 (and_10_out, not_26_out, not_28_out, Instruction[29], not_27_out, not_29_out, not_30_out);
  not not_26 (not_26_out, Instruction[31]);
  not not_27 (not_27_out, Instruction[28]);
  not not_28 (not_28_out, Instruction[30]);
  not not_29 (not_29_out, Instruction[27]);
  not not_30 (not_30_out, Instruction[26]);
  not not_31 (not_31_out, Instruction[4]);
  not not_32 (not_32_out, Instruction[3]);
  not not_33 (not_33_out, Instruction[2]);
  and and_11 (and_11_out, and_5_out, Instruction[5], not_31_out, not_32_out, not_33_out, not_34_out);
  not not_34 (not_34_out, Instruction[0]);
  not not_35 (not_35_out, Instruction[5]);
  and and_12 (and_12_out, and_5_out, not_35_out, Instruction[4], Instruction[3], not_36_out, not_37_out);
  not not_36 (not_36_out, Instruction[2]);
  not not_37 (not_37_out, Instruction[0]);
  or or_3 (imm_sel, and_6_out, j_select, jal_select, shift_select, and_10_out);
  not not_38 (not_38_out, Instruction[3]);
  not not_39 (not_39_out, Instruction[5]);
  not not_40 (not_40_out, Instruction[2]);
  not not_41 (not_41_out, Instruction[0]);
  and and_13 (and_13_out, and_5_out, not_39_out, Instruction[4], not_38_out, not_40_out, not_41_out);
  Demultiplexer demultiplexer_4 (.out0(jr_select), .out1(demultiplexer_4_out1), .in(and_9_out), .sel(Instruction[0]));
  not not_42 (not_42_out, Instruction[4]);
  not not_43 (not_43_out, Instruction[2]);
  not not_44 (not_44_out, Instruction[0]);
  and and_14 (and_14_out, Instruction[5], not_42_out, Instruction[3], and_5_out, not_43_out, Instruction[1], not_44_out);
  not not_45 (not_45_out, Instruction[4]);
  not not_46 (not_46_out, Instruction[5]);
  and and_15 (shift_select, and_5_out, not_46_out, not_45_out, not_47_out, not_48_out, not_49_out);
  or or_4 (jalr_select, demultiplexer_4_out1, and_4_out);
  not not_47 (not_47_out, Instruction[3]);
  not not_48 (not_48_out, Instruction[2]);
  not not_49 (not_49_out, Instruction[0]);
  not not_50 (not_50_out, jr_select);
  or or_5 (or_5_out, jalr_select, jal_select);
  and and_16 (and_16_out, not_50_out, and_5_out);
  or or_6 (op_code[1], and_13_out, or_1_out, and_12_out);
  Demultiplexer demultiplexer_5 (
    .out0(demultiplexer_5_out0), .out1(demultiplexer_5_out1), .in(and_13_out), .sel(Instruction[1]));
  Demultiplexer demultiplexer_6 (
    .out0(demultiplexer_6_out0), .out1(demultiplexer_6_out1), .in(and_11_out), .sel(Instruction[1]));
  Multiplexer #(.width(5)) multiplexer_1 (
    .in0(Instruction[25:21]), .in1(Instruction[20:16]), .out(rs_select), .sel(shift_select));
  Demultiplexer demultiplexer_7 (
    .out0(demultiplexer_7_out0), .out1(demultiplexer_7_out1), .in(shift_select), .sel(Instruction[1]));
  Demultiplexer demultiplexer_8 (
    .out0(demultiplexer_8_out0), .out1(demultiplexer_8_out1), .in(and_12_out), .sel(Instruction[1]));
  or or_7 (or_7_out, or_5_out, lw_select);
  or or_8 (or_8_out, or_2_out, j_select, and_10_out);
  or or_9 (or_9_out, or_7_out, and_11_out, and_13_out, and_16_out, and_14_out, shift_select, and_10_out);
  Multiplexer #(.width(16)) multiplexer_2 (.in1(Instruction[15:0]), .out(imm), .sel(or_8_out));  // open: in0
  not not_51 (not_51_out, lw_select);
  // NOT_Gate not_52 has open pins: in=and_10_out, out=open
  or or_10 (op_code[2], and_13_out, or_1_out, shift_select);
  or or_11 (or_11_out, shift_select, and_14_out, and_13_out, and_11_out);
  Multiplexer #(.width(5)) multiplexer_3 (
    .in1(Instruction[10:6]), .out(shift_amounts), .sel(shift_select));  // open: in0
  Multiplexer #(.width(5)) multiplexer_4 (
    .in0(Instruction[20:16]), .in1(Instruction[15:11]), .out(multiplexer_4_out), .sel(or_12_out));
  or or_12 (or_12_out, or_11_out, or_1_out, and_12_out);
  Multiplexer #(.width(5)) multiplexer_5 (.sel(or_13_out));  // open: in0, in1, out
  or or_13 (or_13_out, and_11_out, and_8_out, and_6_out, and_14_out, and_12_out);
  or or_14 (op_code[0], demultiplexer_7_out1, demultiplexer_5_out0, and_3_out, demultiplexer_8_out1, demultiplexer_6_out1);
  or or_15 (we_regfil, or_9_out, or_1_out);
  Multiplexer #(.width(5)) multiplexer_6 (
    .in0(multiplexer_4_out), .in1({5{1'b1}}), .out(multiplexer_6_out), .sel(jal_select));
  or or_16 (op_code[3], or_1_out, and_14_out);
  Multiplexer #(.width(5)) multiplexer_7 (.in0(multiplexer_6_out), .in1(5'b11010), .out(rd_select), .sel(and_4_out));
  // Probe on undriven

  assign rt_select = Instruction[20:16];

  // Notes on the sheet:
  //   0
  //   |
  //   v
  //   31
  //   clz and clo condition
  //   clz
  //   clo
  //   syscall
  //   lw and sw
  //   j and jal
  //   sw,lw,bne,beq
  //   beq and bne
  //   clo or clz
  //   lw
  //   sw
  //   j
  //   jal
  //   function_code
  //   only for addi
  //   beq
  //   bne
  //   wires for jr and jalr
  //   rs6-10
  //   rt11-15
  //   wire for addi from the function code
  //   wire for mult and div
  //   clz or clo
  //   wire for add and sub
  //   jr
  //   jal
  //   clo only
  //   wire for move from
  //   jalr
  //   wire for shifts
  //   wire for slt
  //   jal,jalr
  //   lw
  //   add
  //   sub
  //   lw,jal,jalr
  //   mfhi
  //   mflo
  //   mult
  //   div
  //   or j
  //   sll
  //   srl
  //   lw,sw,beq,bne,addi
  //   rt
  //   rd
  //   clo or clz
  //   add,sub,addi,moves,shifts,slt,lw
  //   shifts
  //   slt
  //   or multt&div
  //   beq,bne,add,sub,mult,div,slt,lw,sw
  //   clo or clz
  //   rt only have number when it's add_sub, mult_div, and slt
  //   clo or clz
  //   syscall
endmodule

module regfile (
  input  w_e,
  input  [4:0] rs,
  input  [4:0] rd,
  input  [31:0] data_in,
  input  [4:0] rt,
  output [31:0] data_rs,
  output [31:0] data_rt
);

  wire clock_1_out, clock_2_out, demultiplexer_1_out0, demultiplexer_1_out1, demultiplexer_1_out2,
       demultiplexer_1_out3, demultiplexer_1_out4, demultiplexer_1_out5, demultiplexer_1_out6,
       demultiplexer_1_out7, demultiplexer_1_out8, demultiplexer_1_out9, demultiplexer_1_out10,
       demultiplexer_1_out11, demultiplexer_1_out12, demultiplexer_1_out13, demultiplexer_1_out14,
       demultiplexer_1_out15, demultiplexer_1_out16, demultiplexer_1_out17, demultiplexer_1_out18,
       demultiplexer_1_out19, demultiplexer_1_out20, demultiplexer_1_out21, demultiplexer_1_out22,
       demultiplexer_1_out23, demultiplexer_1_out24, demultiplexer_1_out25, demultiplexer_1_out26,
       demultiplexer_1_out27, demultiplexer_1_out28, demultiplexer_1_out29, demultiplexer_1_out30,
       demultiplexer_1_out31;
  wire [31:0] register0_q, register1_q, register2_q, register3_q, register4_q, register5_q, register6_q,
       register7_q, register8_q, register9_q, register10_q, register11_q, register12_q, register13_q,
       register14_q, register15_q, register16_q, register17_q, register18_q, register19_q, register20_q,
       register21_q, register22_q, register23_q, register24_q, register25_q, register26_q, register27_q,
       register28_q, register29_q, register30_q, register31_q;

  Demultiplexer #(.select(5)) demultiplexer_1 (
    .out0(demultiplexer_1_out0), .out1(demultiplexer_1_out1), .out2(demultiplexer_1_out2),
    .out3(demultiplexer_1_out3), .out4(demultiplexer_1_out4), .out5(demultiplexer_1_out5),
    .out6(demultiplexer_1_out6), .out7(demultiplexer_1_out7), .out8(demultiplexer_1_out8),
    .out9(demultiplexer_1_out9), .out10(demultiplexer_1_out10), .out11(demultiplexer_1_out11),
    .out12(demultiplexer_1_out12), .out13(demultiplexer_1_out13), .out14(demultiplexer_1_out14),
    .out15(demultiplexer_1_out15), .out16(demultiplexer_1_out16), .out17(demultiplexer_1_out17),
    .out18(demultiplexer_1_out18), .out19(demultiplexer_1_out19), .out20(demultiplexer_1_out20),
    .out21(demultiplexer_1_out21), .out22(demultiplexer_1_out22), .out23(demultiplexer_1_out23),
    .out24(demultiplexer_1_out24), .out25(demultiplexer_1_out25), .out26(demultiplexer_1_out26),
    .out27(demultiplexer_1_out27), .out28(demultiplexer_1_out28), .out29(demultiplexer_1_out29),
    .out30(demultiplexer_1_out30), .out31(demultiplexer_1_out31), .in(w_e), .sel(rd));
  Clock clock_1 (.out(clock_1_out));
  Register #(.width(32)) register0 (
    .D(data_in), .en(demultiplexer_1_out0), .clk(clock_2_out), .Q(register0_q));  // open: clr
  Clock clock_2 (.out(clock_2_out));
  Register #(.width(32)) register1 (
    .D(data_in), .en(demultiplexer_1_out1), .clk(clock_1_out), .Q(register1_q));  // open: clr
  Register #(.width(32)) register2 (
    .D(data_in), .en(demultiplexer_1_out2), .clk(clock_1_out), .Q(register2_q));  // open: clr
  Register #(.width(32)) register3 (
    .D(data_in), .en(demultiplexer_1_out3), .clk(clock_1_out), .Q(register3_q));  // open: clr
  Register #(.width(32)) register4 (
    .D(data_in), .en(demultiplexer_1_out4), .clk(clock_1_out), .Q(register4_q));  // open: clr
  Register #(.width(32)) register5 (
    .D(data_in), .en(demultiplexer_1_out5), .clk(clock_1_out), .Q(register5_q));  // open: clr
  Register #(.width(32)) register6 (
    .D(data_in), .en(demultiplexer_1_out6), .clk(clock_1_out), .Q(register6_q));  // open: clr
  Register #(.width(32)) register7 (
    .D(data_in), .en(demultiplexer_1_out7), .clk(clock_1_out), .Q(register7_q));  // open: clr
  Register #(.width(32)) register8 (
    .D(data_in), .en(demultiplexer_1_out8), .clk(clock_1_out), .Q(register8_q));  // open: clr
  Register #(.width(32)) register9 (
    .D(data_in), .en(demultiplexer_1_out9), .clk(clock_1_out), .Q(register9_q));  // open: clr
  Register #(.width(32)) register10 (
    .D(data_in), .en(demultiplexer_1_out10), .clk(clock_1_out), .Q(register10_q));  // open: clr
  Register #(.width(32)) register11 (
    .D(data_in), .en(demultiplexer_1_out11), .clk(clock_1_out), .Q(register11_q));  // open: clr
  Register #(.width(32)) register12 (
    .D(data_in), .en(demultiplexer_1_out12), .clk(clock_1_out), .Q(register12_q));  // open: clr
  Register #(.width(32)) register13 (
    .D(data_in), .en(demultiplexer_1_out13), .clk(clock_1_out), .Q(register13_q));  // open: clr
  Register #(.width(32)) register14 (
    .D(data_in), .en(demultiplexer_1_out14), .clk(clock_1_out), .Q(register14_q));  // open: clr
  Register #(.width(32)) register15 (
    .D(data_in), .en(demultiplexer_1_out15), .clk(clock_1_out), .Q(register15_q));  // open: clr
  Register #(.width(32)) register16 (
    .D(data_in), .en(demultiplexer_1_out16), .clk(clock_1_out), .Q(register16_q));  // open: clr
  Register #(.width(32)) register17 (
    .D(data_in), .en(demultiplexer_1_out17), .clk(clock_1_out), .Q(register17_q));  // open: clr
  Register #(.width(32)) register18 (
    .D(data_in), .en(demultiplexer_1_out18), .clk(clock_1_out), .Q(register18_q));  // open: clr
  Register #(.width(32)) register19 (
    .D(data_in), .en(demultiplexer_1_out19), .clk(clock_1_out), .Q(register19_q));  // open: clr
  Register #(.width(32)) register20 (
    .D(data_in), .en(demultiplexer_1_out20), .clk(clock_1_out), .Q(register20_q));  // open: clr
  Register #(.width(32)) register21 (
    .D(data_in), .en(demultiplexer_1_out21), .clk(clock_1_out), .Q(register21_q));  // open: clr
  Register #(.width(32)) register22 (
    .D(data_in), .en(demultiplexer_1_out22), .clk(clock_1_out), .Q(register22_q));  // open: clr
  Register #(.width(32)) register23 (
    .D(data_in), .en(demultiplexer_1_out23), .clk(clock_1_out), .Q(register23_q));  // open: clr
  Register #(.width(32)) register24 (
    .D(data_in), .en(demultiplexer_1_out24), .clk(clock_1_out), .Q(register24_q));  // open: clr
  Register #(.width(32)) register25 (
    .D(data_in), .en(demultiplexer_1_out25), .clk(clock_1_out), .Q(register25_q));  // open: clr
  Register #(.width(32)) register26 (
    .D(data_in), .en(demultiplexer_1_out26), .clk(clock_1_out), .Q(register26_q));  // open: clr
  Register #(.width(32)) register27 (
    .D(data_in), .en(demultiplexer_1_out27), .clk(clock_1_out), .Q(register27_q));  // open: clr
  Register #(.width(32)) register28 (
    .D(data_in), .en(demultiplexer_1_out28), .clk(clock_1_out), .Q(register28_q));  // open: clr
  Register #(.width(32)) register29 (
    .D(data_in), .en(demultiplexer_1_out29), .clk(clock_1_out), .Q(register29_q));  // open: clr
  Register #(.width(32)) register30 (
    .D(data_in), .en(demultiplexer_1_out30), .clk(clock_1_out), .Q(register30_q));  // open: clr
  Register #(.width(32)) register31 (
    .D(data_in), .en(demultiplexer_1_out31), .clk(clock_1_out), .Q(register31_q));  // open: clr
  Multiplexer #(.select(5), .width(32)) multiplexer_1 (
    .in0(register0_q), .in1(register1_q), .in2(register2_q), .in3(register3_q), .in4(register4_q),
    .in5(register5_q), .in6(register6_q), .in7(register7_q), .in8(register8_q), .in9(register9_q),
    .in10(register10_q), .in11(register11_q), .in12(register12_q), .in13(register13_q), .in14(register14_q),
    .in15(register15_q), .in16(register16_q), .in17(register17_q), .in18(register18_q), .in19(register19_q),
    .in20(register20_q), .in21(register21_q), .in22(register22_q), .in23(register23_q), .in24(register24_q),
    .in25(register25_q), .in26(register26_q), .in27(register27_q), .in28(register28_q), .in29(register29_q),
    .in30(register30_q), .in31(register31_q), .out(data_rs), .sel(rs));
  Multiplexer #(.select(5), .width(32)) multiplexer_2 (
    .in0(register0_q), .in1(register1_q), .in2(register2_q), .in3(register3_q), .in4(register4_q),
    .in5(register5_q), .in6(register6_q), .in7(register7_q), .in8(register8_q), .in9(register9_q),
    .in10(register10_q), .in11(register11_q), .in12(register12_q), .in13(register13_q), .in14(register14_q),
    .in15(register15_q), .in16(register16_q), .in17(register17_q), .in18(register18_q), .in19(register19_q),
    .in20(register20_q), .in21(register21_q), .in22(register22_q), .in23(register23_q), .in24(register24_q),
    .in25(register25_q), .in26(register26_q), .in27(register27_q), .in28(register28_q), .in29(register29_q),
    .in30(register30_q), .in31(register31_q), .out(data_rt), .sel(rt));
endmodule

module TerminalController (
  input  [31:0] DataBus_in,
  input  [15:0] Address_in,
  input  DataBus_we,
  output [6:0] DataBus_out,
  output Terminal_we
);

  wire comparator_1_eq;
  wire [31:0] multiplexer_1_out;

  Comparator #(.width(16)) comparator_1 (.a(Address_in), .b(16'h70), .eq(comparator_1_eq));  // open: gt, lt
  and and_1 (Terminal_we, comparator_1_eq, DataBus_we);
  Multiplexer #(.width(32)) multiplexer_1 (
    .in0({32{1'b0}}), .in1(DataBus_in), .out(multiplexer_1_out), .sel(Terminal_we));
  Bit_Extender #(.in_width(32), .out_width(7)) bit_extender_1 (.in(multiplexer_1_out), .out(DataBus_out));
endmodule

module clo (
  input  [31:0] in_1,
  output [5:0] out_2
);

  wire comparator_1_eq;
  wire [4:0] bitfinder_1_index, subtractor_1_out;
  wire [5:0] bit_extender_1_out;
  wire [31:0] not_1_out;

  assign not_1_out = ~in_1;  // NOT_Gate not_1, 32 bits wide
  BitFinder #(.\type ("high0"), .width(32)) bitfinder_1 (.in(in_1), .index(bitfinder_1_index));  // open: found
  Comparator #(.width(32)) comparator_1 (.a(not_1_out), .b({32{1'b0}}), .eq(comparator_1_eq));  // open: gt, lt
  Subtractor #(.width(5)) subtractor_1 (
    .a({5{1'b1}}), .b(bitfinder_1_index), .out(subtractor_1_out));  // open: bin, bout
  assign bit_extender_1_out = {{1{1'b0}}, subtractor_1_out};  // Bit_Extender bit_extender_1
  Multiplexer #(.width(6)) multiplexer_1 (
    .in0(bit_extender_1_out), .in1(6'b100000), .out(out_2), .sel(comparator_1_eq));
endmodule

module clz (
  input  [31:0] in_1,
  output [5:0] out_2
);

  wire comparator_1_eq;
  wire [4:0] bitfinder_1_index, subtractor_1_out;
  wire [5:0] bit_extender_1_out;

  BitFinder #(.\type ("high1"), .width(32)) bitfinder_1 (.in(in_1), .index(bitfinder_1_index));  // open: found
  Comparator #(.width(32)) comparator_1 (.a(in_1), .b({32{1'b0}}), .eq(comparator_1_eq));  // open: gt, lt
  Subtractor #(.width(5)) subtractor_1 (
    .a({5{1'b1}}), .b(bitfinder_1_index), .out(subtractor_1_out));  // open: bin, bout
  assign bit_extender_1_out = {{1{1'b0}}, subtractor_1_out};  // Bit_Extender bit_extender_1
  Multiplexer #(.width(6)) multiplexer_1 (
    .in0(bit_extender_1_out), .in1(6'b100000), .out(out_2), .sel(comparator_1_eq));
endmodule

module JoystickController (
  input  [3:0] Xcoord,
  input  [3:0] Ycoord,
  input  [15:0] Address,
  output [31:0] Databus,
  output JoystickWrite
);

  wire comparator_1_eq, comparator_2_eq;
  wire [3:0] multiplexer_1_out;

  Comparator #(.width(16)) comparator_1 (.a(Address), .b(16'h30), .eq(comparator_1_eq));  // open: gt, lt
  Comparator #(.width(16)) comparator_2 (.a(Address), .b(16'h34), .eq(comparator_2_eq));  // open: gt, lt
  Multiplexer #(.width(4)) multiplexer_1 (.in0(Xcoord), .in1(Ycoord), .out(multiplexer_1_out), .sel(comparator_2_eq));
  assign Databus = {{28{1'b0}}, multiplexer_1_out};  // Bit_Extender bit_extender_1
  or or_1 (JoystickWrite, comparator_1_eq, comparator_2_eq);
endmodule
